# Fritzing sketch Camera_Board (saved by Fritzing 0.9.3b)
circuit board: 7cm x 2.3cm
breadboards: 1

parts:
  J1 = Screw terminal - 2 pins [package=THT]
  U2 = Voltage Regulator - 5V [package="TO220 [THT]"]
  D1 = Schottky Diode [part_number=1N5817 package="300 mil [THT]"]
  C1 = Electrolytic Capacitor [capacitance=1µF package="100 mil [THT, electrolytic]"]
  C2 = Electrolytic Capacitor [capacitance=1µF package="100 mil [THT, electrolytic]"]
  J2 = Screw terminal - 2 pins [package=THT]
  R1 = Resistor [tolerance=±5% resistance=220 package=THT]
  LED1 = LED - 5mm [color="Red (633nm)" package="5 mm [THT]"]

nets:
  N1: J1.pin1, U2.GND, C1.-, C2.-, J2.pin2, LED1.cathode
  N2: J1.pin2, D1.anode
  N3: U2.input_voltage, D1.cathode, C1.+
  N4: U2.output_voltage, C2.+, J2.pin1, R1.Pin_0
  N5: R1.Pin_1, LED1.anode
