# Fritzing sketch Transistor_H_Bridge (saved by Fritzing 0.9.3b)
breadboards: 1

parts:
  Q1 = NPN-Transistor [package="TO92 [THT]"]
  Q2 = NPN-Transistor [package="TO92 [THT]"]
  Q3 = NPN-Transistor [package="TO92 [THT]"]
  Q4 = NPN-Transistor [package="TO92 [THT]"]
  Part1 = Arduino Uno (Rev3)
  J1 = Camdenboss CTB0158-4 [part_number=CTB0158-4 package=THT]

nets:
  N1: Q1.E, Q4.E, J1.pin1
  N2: Q1.B, Part1.D9_PWM
  N3: Q1.C, Q3.C, J1.pin3
  N4: Q2.E, Q3.E, J1.pin2
  N5: Q2.B, Part1.D8
  N6: Q2.C, Q4.C, J1.pin4
  N7: Q3.B, Part1.D7
  N8: Q4.B, Part1.D6_PWM
