# Fritzing sketch Underwater_Circuit_Final (saved by Fritzing 0.9.3b)
circuit board: 19.2623cm x 8.77897cm
breadboards: 1

parts:
  J1 = Screw terminal - 2 pins [package=THT]
  J2 = Screw terminal - 2 pins [package=THT]
  J3 = Screw terminal - 2 pins [package=THT]
  J4 = Screw terminal - 2 pins [package=THT]
  J5 = Screw terminal - 2 pins [package=THT]
  J6 = Screw terminal - 2 pins [package=THT]
  U1 = RJ45 Jack [package=rj45-8]
  J7 = Screw terminal - 2 pins [package=THT]
  J8 = Screw terminal - 2 pins [package=THT]
  J9 = Screw terminal - 2 pins [package=THT]
  J10 = Screw terminal - 2 pins [package=THT]
  J11 = Screw terminal - 2 pins [package=THT]
  J12 = Screw terminal - 2 pins [package=THT]
  J15 = Screw terminal - 2 pins [package=THT]
  J16 = Screw terminal - 2 pins [package=THT]
  J17 = Screw terminal - 2 pins [package=THT]
  Part1 = Arduino Mega ADK (Rev3)
  LED1 = smd LED [color="Red (633nm)" package="1206 [SMD]"]
  LED2 = smd LED [color="Red (633nm)" package="1206 [SMD]"]
  R1 = Resistor [tolerance=±5% resistance=220 package=THT]
  R2 = Resistor [tolerance=±5% resistance=220 package=THT]
  R3 = Resistor [tolerance=±5% resistance=220 package=THT]
  J18 = Screw terminal - 2 pins [package=THT]
  J19 = Screw terminal - 2 pins [package=THT]
  J20 = Screw terminal - 2 pins [package=THT]
  R4 = Resistor [tolerance=±5% resistance=220 package=THT]
  GY1 = MPU-6050 Board GY-521 [form="♀ (female)" package=THT]
  Part2 = Arduino Nano (Rev3.0) (ICSP)
  D1 = Diode [package=diode-1n4148]
  U2 = Voltage Regulator - 5V [package="TO220 [THT]"]
  C1 = Electrolytic Capacitor [capacitance=1µF package="100 mil [THT, electrolytic]"]
  C2 = Electrolytic Capacitor [capacitance=1µF package="100 mil [THT, electrolytic]"]
  R5 = Resistor [tolerance=±5% resistance=220 package=THT]
  LED3 = LED - 5mm [color="Red (633nm)" package="5 mm [THT]"]
  J21 = Screw terminal - 2 pins [package=THT]

nets (from the pcb view):
  N1: J1.pin1, Part1.D7_PWM
  N2: J1.pin2, Part1.D27
  N3: J2.pin1, Part1.D29
  N4: J2.pin2, Part1.D6_PWM
  N5: J3.pin1, Part1.D31
  N6: J3.pin2, Part1.D33
  N7: J4.pin1, Part1.D5_PWM
  N8: J4.pin2, Part1.D35
  N9: J5.pin1, Part1.D37
  N10: J5.pin2, Part1.D4_PWM
  N11: J6.pin1, Part1.D39
  N12: J6.pin2, Part1.D41
  N13: U1.2, Part1.D20/SDA, R4.Pin_0
  N14: U1.4, Part1.D21/SCL, R3.Pin_1
  GND: U1.5, J7.pin2, J9.pin1, J10.pin2, J12.pin1, Part1.GND, R1.Pin_0, R2.Pin_1, GY1.pin2, Part2.GND, J21.pin1, J21.pin2
  N15: U1.8, J18.pin1
  N16: J7.pin1, J8.pin2, J10.pin1, J11.pin2, Part1.IOREF, Part1.5V, LED1.cathode, LED2.cathode, R3.Pin_0, R4.Pin_1
  N17: J8.pin1, Part1.D13_PWM
  N18: J9.pin2, Part1.D12_PWM
  N19: J11.pin1, Part1.D11_PWM
  N20: J12.pin2, Part1.D10_PWM
  N21: J15.pin1, Part1.D3_PWM
  N22: J15.pin2, Part1.D43
  N23: J16.pin1, Part1.D45
  N24: J16.pin2, Part1.D2_PWM
  N25: J17.pin1, Part1.D47
  N26: J17.pin2, Part1.D49
  N27: Part1.D9_PWM, Part2.D11/MOSI
  N28: Part1.D8_PWM, Part2.D10
  N29: LED1.anode, R2.Pin_0
  N30: LED2.anode, R1.Pin_1
  N31: J19.pin1, U2.input_voltage, C2.+, LED3.cathode
  N32: J19.pin2, J20.pin2, U2.GND, C1.-, C2.-, R5.Pin_0
  N33: J20.pin1, D1.A
  N34: GY1.pin1, Part2.5V
  N35: GY1.pin3, Part2.A5
  N36: GY1.pin4, Part2.A4
  N37: GY1.pin5, Part2.D2
  N38: D1.C, U2.output_voltage, C1.+
  N39: R5.Pin_1, LED3.anode

notes:
  Top to bottom:
  i from 0 to 6
  Motor i - analog data
  Motor i - forward side
  Motor i - backward side
  Top to bottom:
  Arm-x 5v,gnd,data
  Arm-y 5v,gnd,data
  Cam-x 5v,gnd,data
  Cam-y 5v,gnd,data
  Gyro GND,TX,RX (10,11) -> (7,6)
  Power
  12 Volts
  GND
  5V
  Gnd
  Camera data to ethernet pin + GND
  Null
  Ethernet:
  SDA
  SCL
  Camera Data , GND
  GND for Potentiometer

custom parts:
  MPU-6050 Board GY-521: Acelerometro y Giroscopio MPU-6050 Board GY-521
