# Fritzing sketch VR_Circuit (saved by Fritzing 0.9.3b)
circuit board: 5.52802cm x 4.25618cm
breadboards: 1

parts:
  GY1 = MPU-6050 Board GY-521 [form="♀ (female)" package=THT]
  Part1 = Arduino Nano (Rev3.0)
  U1 = RJ45 Jack [package=rj45-8]
  LED1 = smd LED [color="Red (633nm)" package="0805 [SMD]"]
  R1 = Resistor [tolerance=±5% resistance=220 package=THT]

nets (from the pcb view):
  N1: GY1.pin1, Part1.5V
  N2: GY1.pin2, Part1.GND, U1.4, R1.Pin_1
  N3: GY1.pin3, Part1.A5
  N4: GY1.pin4, Part1.A4
  N5: GY1.pin5, Part1.D2
  N6: Part1.D8, LED1.cathode
  N7: Part1.D10, U1.8
  N8: Part1.D11/MOSI, U1.2
  N9: LED1.anode, R1.Pin_0

custom parts:
  MPU-6050 Board GY-521: Acelerometro y Giroscopio MPU-6050 Board GY-521
